// Logisim project Etienne Laramee CS306 Assignment 1.circ as structural Verilog
module Half_Adder (
  input  A,
  input  B,
  output S,
  output C
);

  xor xor_1 (S, A, B);
  and and_1 (C, A, B);
endmodule

module Full_Adder (
  input  C_in,
  input  A,
  input  B,
  output Sum,
  output C_out
);

  wire HA_1_c, HA_1_s, HA_2_c;

  Half_Adder HA_1 (.A(A), .B(B), .S(HA_1_s), .C(HA_1_c));
  Half_Adder HA_2 (.A(C_in), .B(HA_1_s), .S(Sum), .C(HA_2_c));
  or or_1 (C_out, HA_2_c, HA_1_c);
endmodule

module _8_bit_ADD_SUB (
  input  Add_Subtract_Control,
  input  [7:0] A,
  input  [7:0] B,
  output [7:0] Result,
  output Carry_out,
  output Overflow
);

  wire and_1_out, and_2_out, Full_Adder_1_c_out, Full_Adder_2_c_out, Full_Adder_3_c_out, Full_Adder_4_c_out,
       Full_Adder_5_c_out, Full_Adder_6_c_out, Full_Adder_7_c_out, xor_1_out, xor_2_out, xor_3_out,
       xor_4_out, xor_5_out, xor_6_out, xor_7_out, xor_8_out;

  xor xor_1 (xor_1_out, Add_Subtract_Control, B[0]);
  xor xor_2 (xor_2_out, Add_Subtract_Control, B[1]);
  xor xor_3 (xor_3_out, Add_Subtract_Control, B[2]);
  xor xor_4 (xor_4_out, Add_Subtract_Control, B[3]);
  xor xor_5 (xor_5_out, Add_Subtract_Control, B[4]);
  xor xor_6 (xor_6_out, Add_Subtract_Control, B[5]);
  xor xor_7 (xor_7_out, Add_Subtract_Control, B[6]);
  xor xor_8 (xor_8_out, Add_Subtract_Control, B[7]);
  Full_Adder Full_Adder_1 (
    .C_in(Add_Subtract_Control), .A(A[0]), .B(xor_1_out), .Sum(Result[0]), .C_out(Full_Adder_1_c_out));
  Full_Adder Full_Adder_2 (
    .C_in(Full_Adder_1_c_out), .A(A[1]), .B(xor_2_out), .Sum(Result[1]), .C_out(Full_Adder_2_c_out));
  Full_Adder Full_Adder_3 (
    .C_in(Full_Adder_2_c_out), .A(A[2]), .B(xor_3_out), .Sum(Result[2]), .C_out(Full_Adder_3_c_out));
  Full_Adder Full_Adder_4 (
    .C_in(Full_Adder_3_c_out), .A(A[3]), .B(xor_4_out), .Sum(Result[3]), .C_out(Full_Adder_4_c_out));
  Full_Adder Full_Adder_5 (
    .C_in(Full_Adder_4_c_out), .A(A[4]), .B(xor_5_out), .Sum(Result[4]), .C_out(Full_Adder_5_c_out));
  Full_Adder Full_Adder_6 (
    .C_in(Full_Adder_5_c_out), .A(A[5]), .B(xor_6_out), .Sum(Result[5]), .C_out(Full_Adder_6_c_out));
  Full_Adder Full_Adder_7 (
    .C_in(Full_Adder_6_c_out), .A(A[6]), .B(xor_7_out), .Sum(Result[6]), .C_out(Full_Adder_7_c_out));
  Full_Adder Full_Adder_8 (.C_in(Full_Adder_7_c_out), .A(A[7]), .B(xor_8_out), .Sum(Result[7]), .C_out(Carry_out));
  and and_1 (and_1_out, Result[7], ~xor_8_out, ~A[7]);  // AND_Gate
  or or_1 (Overflow, and_1_out, and_2_out);
  and and_2 (and_2_out, ~Result[7], xor_8_out, A[7]);  // AND_Gate
endmodule

module _8_bit_OR (
  input  [7:0] A,
  input  [7:0] B,
  output [7:0] Result
);

  or or_1 (Result[0], A[0], B[0]);
  or or_2 (Result[1], A[1], B[1]);
  or or_3 (Result[2], A[2], B[2]);
  or or_4 (Result[3], A[3], B[3]);
  or or_5 (Result[4], A[4], B[4]);
  or or_6 (Result[5], A[5], B[5]);
  or or_7 (Result[6], A[6], B[6]);
  or or_8 (Result[7], A[7], B[7]);
endmodule

module _8_bit_AND (
  input  [7:0] A,
  input  [7:0] B,
  output [7:0] Result
);

  and and_1 (Result[0], A[0], B[0]);
  and and_2 (Result[1], A[1], B[1]);
  and and_3 (Result[2], A[2], B[2]);
  and and_4 (Result[3], A[3], B[3]);
  and and_5 (Result[4], A[4], B[4]);
  and and_6 (Result[5], A[5], B[5]);
  and and_7 (Result[6], A[6], B[6]);
  and and_8 (Result[7], A[7], B[7]);
endmodule

module ALU (
  input  [7:0] R1,
  input  [7:0] R2,
  input  [3:0] OpCode,
  output [7:0] R_out,
  output ZERO,
  output Negative,
  output Carry,
  output Overflow,
  output Greater_Than,
  output Equal,
  output Less_Than
);

  wire Add_Sub_carry_out, Add_Sub_overflow, and_2_out, and_3_out, and_4_out, INC_DEC_carry_borow;
  wire [2:0] Compare_gt;
  wire [7:0] Add_Sub_result, AND_result, INC_DEC_result, NOT_result, OR_result, Shift_L_result,
       Shift_R_result;

  _8_bit_OR OR (.A(R1), .B(R2), .Result(OR_result));
  _8_bit_AND AND (.A(R1), .B(R2), .Result(AND_result));
  _8_bit_ADD_SUB Add_Sub (
    .Add_Subtract_Control(OpCode[0]), .Result(Add_Sub_result), .Carry_out(Add_Sub_carry_out),
    .Overflow(Add_Sub_overflow), .A(R1), .B(R2));
  _8_bit_INC_DEC INC_DEC (.A(R1), .Control(OpCode[0]), .Result(INC_DEC_result), .Carry_Borow(INC_DEC_carry_borow));
  _8_bit_CMP Compare (.A(R1), .B(R2), .GT(Compare_gt[0]), .EQ(Compare_gt[1]), .LT(Compare_gt[2]));
  _8_bit_NOT NOT (.A(R1), .Result(NOT_result));
  _8_bit_SFTL Shift_L (.A(R1), .Result(Shift_L_result));
  _8_bit_SFTR Shift_R (.A(R1), .Result(Shift_R_result));
  Multiplexer #(.select(4), .width(8), .enable("false")) multiplexer_1 (
    .in0(OR_result), .in1(AND_result), .in2(Add_Sub_result), .in3(Add_Sub_result), .in4(INC_DEC_result),
    .in5(INC_DEC_result), .in7(NOT_result), .in12(Shift_L_result), .in13(Shift_R_result),
    .out({Negative, R_out[6:0]}), .sel(OpCode));  // open: in6, in8, in9, in10, in11, in14, in15
  and and_2 (and_2_out, OpCode[3], ~OpCode[2], ~OpCode[1], ~OpCode[0]);  // AND_Gate
  and and_3 (and_3_out, OpCode[1], ~OpCode[2], Add_Sub_carry_out);  // AND_Gate
  and and_4 (and_4_out, INC_DEC_carry_borow, ~OpCode[1], OpCode[2]);  // AND_Gate
  and and_5 (Overflow, Add_Sub_overflow, ~OpCode[2], OpCode[1]);  // AND_Gate
  nor nor_1 (ZERO, R_out[0], R_out[1], R_out[2], R_out[3], R_out[4], R_out[5], R_out[6], Negative);
  or or_2 (Carry, and_3_out, and_4_out);
  and and_6 (Greater_Than, Compare_gt[0], and_2_out);
  and and_7 (Equal, Compare_gt[1], and_2_out);
  and and_8 (Less_Than, Compare_gt[2], and_2_out);

  assign R_out[7] = Negative;

  // Notes on the sheet:
  //   0000
  //   0001
  //   0010
  //   0011
  //   0100
  //   0101
  //   0110
  //   0111
  //   1000
  //   1001
  //   1010
  //   1011
  //   1100
  //   1101
  //   OR
  //   AND
  //   ADD
  //   SUB
  //   INC
  //   DEC
  //   NOT
  //   MUL
  //   CMP
  //   XOR
  //   NAND
  //   TCPL
  //   SFTL
  //   SFTR
  //   Not Implemented
  //   Not Implemented
  //   Not Implemented
  //   Not Implemented
  //   Flags
endmodule

module _8_bit_INC_DEC (
  input  Control,
  input  [7:0] A,
  output Carry_Borow,
  output [7:0] Result
);

  wire n8_bit_half_adder_half_subtractor_1_carry_borrow, n8_bit_half_adder_half_subtractor_2_carry_borrow,
       n8_bit_half_adder_half_subtractor_3_carry_borrow, n8_bit_half_adder_half_subtractor_4_carry_borrow,
       n8_bit_half_adder_half_subtractor_5_carry_borrow, n8_bit_half_adder_half_subtractor_6_carry_borrow,
       n8_bit_half_adder_half_subtractor_8_carry_borrow;

  _8_bit_Half_Adder_Half_Subtractor u_8_bit_half_adder_half_subtractor_1 (
    .A(A[0]), .B(1'b1), .Control(Control), .Sum_Diff(Result[0]),
    .Carry_Borrow(n8_bit_half_adder_half_subtractor_1_carry_borrow));
  _8_bit_Half_Adder_Half_Subtractor u_8_bit_half_adder_half_subtractor_2 (
    .A(A[1]), .B(n8_bit_half_adder_half_subtractor_1_carry_borrow), .Control(Control), .Sum_Diff(Result[1]),
    .Carry_Borrow(n8_bit_half_adder_half_subtractor_2_carry_borrow));
  _8_bit_Half_Adder_Half_Subtractor u_8_bit_half_adder_half_subtractor_3 (
    .A(A[2]), .B(n8_bit_half_adder_half_subtractor_2_carry_borrow), .Control(Control), .Sum_Diff(Result[2]),
    .Carry_Borrow(n8_bit_half_adder_half_subtractor_3_carry_borrow));
  _8_bit_Half_Adder_Half_Subtractor u_8_bit_half_adder_half_subtractor_4 (
    .A(A[3]), .B(n8_bit_half_adder_half_subtractor_3_carry_borrow), .Control(Control), .Sum_Diff(Result[3]),
    .Carry_Borrow(n8_bit_half_adder_half_subtractor_4_carry_borrow));
  _8_bit_Half_Adder_Half_Subtractor u_8_bit_half_adder_half_subtractor_5 (
    .A(A[4]), .B(n8_bit_half_adder_half_subtractor_4_carry_borrow), .Control(Control), .Sum_Diff(Result[4]),
    .Carry_Borrow(n8_bit_half_adder_half_subtractor_5_carry_borrow));
  _8_bit_Half_Adder_Half_Subtractor u_8_bit_half_adder_half_subtractor_6 (
    .A(A[5]), .B(n8_bit_half_adder_half_subtractor_5_carry_borrow), .Control(Control), .Sum_Diff(Result[5]),
    .Carry_Borrow(n8_bit_half_adder_half_subtractor_6_carry_borrow));
  _8_bit_Half_Adder_Half_Subtractor u_8_bit_half_adder_half_subtractor_7 (
    .A(A[7]), .B(n8_bit_half_adder_half_subtractor_8_carry_borrow), .Control(Control), .Sum_Diff(Result[7]),
    .Carry_Borrow(Carry_Borow));
  _8_bit_Half_Adder_Half_Subtractor u_8_bit_half_adder_half_subtractor_8 (
    .A(A[6]), .B(n8_bit_half_adder_half_subtractor_6_carry_borrow), .Control(Control), .Sum_Diff(Result[6]),
    .Carry_Borrow(n8_bit_half_adder_half_subtractor_8_carry_borrow));
endmodule

module _8_bit_Half_Adder_Half_Subtractor (
  input  Control,
  input  A,
  input  B,
  output Sum_Diff,
  output Carry_Borrow
);

  wire and_1_out, and_2_out;

  xor xor_1 (Sum_Diff, A, B);
  and and_1 (and_1_out, ~A, B, Control);  // AND_Gate
  or or_1 (Carry_Borrow, and_1_out, and_2_out);
  and and_2 (and_2_out, A, B, ~Control);  // AND_Gate
endmodule

module _8_bit_CMP (
  input  [7:0] A,
  input  [7:0] B,
  output GT,
  output EQ,
  output LT
);

  wire and_1_out, and_2_out, and_3_out, and_4_out, and_5_out, and_6_out, and_7_out, and_8_out, and_9_out,
       and_10_out, and_11_out, and_12_out, and_13_out, and_14_out, and_15_out, and_16_out, xnor_1_out,
       xnor_2_out, xnor_3_out, xnor_4_out, xnor_5_out, xnor_6_out, xnor_7_out, xnor_8_out;

  xnor xnor_1 (xnor_1_out, A[0], B[0]);
  xnor xnor_2 (xnor_2_out, A[1], B[1]);
  xnor xnor_3 (xnor_3_out, A[2], B[2]);
  xnor xnor_4 (xnor_4_out, A[3], B[3]);
  xnor xnor_5 (xnor_5_out, A[4], B[4]);
  xnor xnor_6 (xnor_6_out, A[5], B[5]);
  xnor xnor_7 (xnor_7_out, A[6], B[6]);
  xnor xnor_8 (xnor_8_out, A[7], B[7]);
  and and_1 (and_1_out, ~B[0], A[0], xnor_2_out, xnor_3_out, xnor_4_out, xnor_5_out, xnor_6_out, xnor_7_out, xnor_8_out);  // AND_Gate
  and and_2 (and_2_out, ~B[1], A[1], xnor_3_out, xnor_4_out, xnor_5_out, xnor_6_out, xnor_7_out, xnor_8_out);  // AND_Gate
  and and_3 (and_3_out, ~B[2], A[2], xnor_4_out, xnor_5_out, xnor_6_out, xnor_7_out, xnor_8_out);  // AND_Gate
  and and_4 (and_4_out, ~B[3], A[3], xnor_5_out, xnor_6_out, xnor_7_out, xnor_8_out);  // AND_Gate
  and and_5 (and_5_out, ~B[4], A[4], xnor_6_out, xnor_7_out, xnor_8_out);  // AND_Gate
  and and_6 (and_6_out, ~B[5], A[5], xnor_7_out, xnor_8_out);  // AND_Gate
  and and_7 (and_7_out, ~B[6], A[6], xnor_8_out);  // AND_Gate
  and and_8 (and_8_out, ~B[7], A[7]);  // AND_Gate
  and and_9 (and_9_out, ~A[7], B[7]);  // AND_Gate
  and and_10 (and_10_out, ~A[6], B[6], xnor_8_out);  // AND_Gate
  and and_11 (and_11_out, ~A[5], B[5], xnor_8_out, xnor_7_out);  // AND_Gate
  and and_12 (and_12_out, ~A[4], B[4], xnor_8_out, xnor_7_out, xnor_6_out);  // AND_Gate
  and and_13 (and_13_out, ~A[3], B[3], xnor_8_out, xnor_7_out, xnor_6_out, xnor_5_out);  // AND_Gate
  and and_14 (and_14_out, ~A[2], B[2], xnor_8_out, xnor_7_out, xnor_6_out, xnor_5_out, xnor_4_out);  // AND_Gate
  and and_15 (and_15_out, ~A[1], B[1], xnor_8_out, xnor_7_out, xnor_6_out, xnor_5_out, xnor_4_out, xnor_3_out);  // AND_Gate
  and and_16 (and_16_out, ~A[0], B[0], xnor_8_out, xnor_7_out, xnor_6_out, xnor_5_out, xnor_4_out, xnor_3_out, xnor_2_out);  // AND_Gate
  and and_17 (EQ, xnor_1_out, xnor_2_out, xnor_3_out, xnor_4_out, xnor_5_out, xnor_6_out, xnor_7_out, xnor_8_out);
  or or_1 (GT, and_1_out, and_2_out, and_3_out, and_4_out, and_5_out, and_6_out, and_7_out, and_8_out);
  or or_2 (LT, and_9_out, and_10_out, and_11_out, and_12_out, and_13_out, and_14_out, and_15_out, and_16_out);
endmodule

module _8_bit_NOT (
  input  [7:0] A,
  output [7:0] Result
);

  not not_1 (Result[0], A[0]);
  not not_2 (Result[1], A[1]);
  not not_3 (Result[2], A[2]);
  not not_4 (Result[3], A[3]);
  not not_5 (Result[4], A[4]);
  not not_6 (Result[5], A[5]);
  not not_7 (Result[6], A[6]);
  not not_8 (Result[7], A[7]);
endmodule

module _8_bit_SFTL (
  input  [7:0] A,
  output [7:0] Result
);


  assign Result = {A[6:0], 1'b0};
endmodule

module _8_bit_SFTR (
  input  [7:0] A,
  output [7:0] Result
);


  assign Result = {1'b0, A[7:1]};
endmodule
